# Fritzing sketch scheme (saved by Fritzing 0.7.7b)
breadboards: 1

parts:
  Nano1 = Arduino Nano v2.3
  Parte1 = Bluetooth Mate Silver
  LED1 = LED - 5mm [color="Red (633nm)" package="5 mm [THT]"]

nets:
  N1: Nano1.D0RX, Parte1.TX_5V
  N2: Nano1.RST, Parte1.RX_5V
  GND: Nano1.GND, Parte1.GND
  N3: Nano1.D8, LED1.anode
  +5V: Nano1.+5V, Parte1.VCC
